# Fritzing sketch fritzing_colorbeat (saved by Fritzing 0.9.10b)
breadboards: 1

parts:
  Composant1 = Arduino Uno (Rev3)
  U2 = WS2812 RGB LED strip
  PART2 = Sound Detector
  S1 = Pushbutton [package="[THT]"]
  R1 = Rotary Potentiometer (Small) [maximum_resistance=100kΩ knob_status=50% power=0.5W package=THT]
  R2 = Rotary Potentiometer (Small) [maximum_resistance=100kΩ knob_status=50% power=0.5W package=THT]
  R3 = Rotary Potentiometer (Small) [maximum_resistance=100kΩ knob_status=50% power=0.5W package=THT]
  R4 = Resistor [tolerance=±5% resistance=10k package="1206 [SMD]"]
  S2 = Pushbutton [package="[THT]"]
  R5 = Resistor [tolerance=±5% resistance=10k package="1206 [SMD]"]

nets:
  N1: Composant1.A0, PART2.ENVELOPE
  N2: Composant1.A1, R3.wiper
  N3: Composant1.A2, R2.wiper
  N4: Composant1.A3, R1.wiper
  GND: Composant1.GND, U2.GND, PART2.GND, S1.Pin_1, S1.Pin_2, R1.leg1, R2.leg1, R3.leg1, S2.Pin_1, S2.Pin_2
  N5: Composant1.D5_PWM, S2.Pin_3, S2.Pin_4, R5.Pin_1
  N6: Composant1.D6_PWM, U2.DIN
  N7: Composant1.D7, S1.Pin_3, S1.Pin_4, R4.Pin_1
  VCC: Composant1.5V, U2.VCC, PART2.VCC, R1.leg2, R2.leg2, R3.leg2, R4.Pin_0, R5.Pin_0

custom parts:
  WS2812 RGB LED strip: WS2812 strip
  Sound Detector: Electret microphone with multiple outputs. - First output is the actual audio - Second output is the amplitude envelope - Third output is a binary "sound present" indication - high while sound is present, low otherwise. Visit sparkfun.com for more documentations.
